# Fritzing sketch assignment-1 (saved by Fritzing 0.9.3b)
breadboards: 1

parts:
  U1 = NodeMCU V3.0
  LED1 = smd LED [color="Red (633nm)" package="0805 [SMD]"]
  R1 = Resistor [tolerance=±5% resistance=220 package=THT]

nets:
  N1: U1.D0, R1.Pin_0
  N2: U1.GND#6, U1.GND#13, U1.GND#16, U1.GND#33, LED1.cathode
  N3: LED1.anode, R1.Pin_1

custom parts:
  NodeMCU V3.0: ESP8266 based NodeMCU
