# Fritzing sketch read-a-button (saved by Fritzing 0.9.3b)
breadboards: 1

parts:
  U1 = NodeMCU V3.0
  S1 = Pushbutton [package="[SMD]"]
  R1 = Resistor [tolerance=±5% resistance=10k package=THT]

nets (from the schematic view):
  N1: U1.D2, S1.Pin_1, S1.Pin_2, R1.Pin_1
  N2: U1.GND#6, U1.GND#13, U1.GND#16, U1.GND#33, S1.Pin_3, S1.Pin_4
  N3: U1.Vin, R1.Pin_0

custom parts:
  NodeMCU V3.0: ESP8266 based NodeMCU
