# Fritzing sketch read-temperature (saved by Fritzing 0.9.3b)
breadboards: 1

parts:
  U1 = NodeMCU V3.0
  R1 = Resistor [tolerance=±5% resistance=1k package=THT]
  RHT1 = Humidity and Temperature Sensor RHT03

nets:
  N1: U1.D1, R1.Pin_1, RHT1.Data-signal
  N2: U1.GND#6, U1.GND#13, U1.GND#16, U1.GND#33, RHT1.GND_2
  VIN: U1.Vin, R1.Pin_0, RHT1.Vcc

custom parts:
  NodeMCU V3.0: ESP8266 based NodeMCU
